# Fritzing sketch CAN-BUS-Weichendecoder (saved by Fritzing 0.9.4)
circuit board: 12.104cm x 7.80865cm
breadboards: 3

parts:
  M1 = Niren can bus module [package=THT]
  IC1 = ULN2803A [package=THT]
  IC2 = ULN2803A [package=THT]
  U1 = PCF8574 [package="DIP16 [THT]"]
  U2 = PCF8574 [package="DIP16 [THT]"]
  U3 = PCF8574 [package="DIP16 [THT]"]
  IC3 = ULN2803A [package=THT]
  IC4 = ULN2803A [package=THT]
  IC5 = ULN2803A [package=THT]
  R2 = Resistor [tolerance=±5% resistance=220 package=THT]
  R3 = Resistor [tolerance=±5% resistance=220 package=THT]
  R4 = Resistor [tolerance=±5% resistance=220 package=THT]
  R5 = Resistor [tolerance=±5% resistance=220 package=THT]
  Bauteil1 = Arduino Nano (Rev3.0)

nets:
  VCC: M1.pin1, U1.VCC, U2.VCC, U3.VCC, Bauteil1.5V
  GND: M1.pin2, U1.A0, U1.A1, U1.A2, U1.GND, U2.A0, U2.A1, U2.GND, U3.A0, U3.A2, U3.GND, IC3.0V, Bauteil1.GND
  N1: M1.pin3, Bauteil1.D10
  N2: M1.pin4, Bauteil1.D12/MISO
  N3: M1.pin5, Bauteil1.D11/MOSI
  N4: M1.pin6, Bauteil1.D13/SCK
  N5: M1.pin7, Bauteil1.D2
  N6: IC1.In_1, Bauteil1.D9
  N7: IC1.In_2, Bauteil1.D8
  N8: IC1.In_3, Bauteil1.D7
  N9: IC1.In_4, Bauteil1.D6
  N10: IC1.In_5, Bauteil1.D5
  N11: IC1.In_6, Bauteil1.D4
  N12: IC1.In_7, Bauteil1.A0
  N13: IC1.In_8, Bauteil1.A1
  N14: IC2.In_1, Bauteil1.A2
  N15: IC2.In_2, Bauteil1.A3
  N16: U1.P0, IC3.In_8
  N17: U1.P1, IC3.In_7
  N18: U1.P2, IC3.In_6
  N19: U1.P3, IC3.In_5
  N20: U1.P4, IC3.In_4
  N21: U1.P5, IC3.In_3
  N22: U1.P6, IC3.In_2
  N23: U1.P7, IC3.In_1
  N24: U1.SCL, U2.SCL, U3.SCL, Bauteil1.A5
  N25: U1.SDA, U2.SDA, U3.SDA, Bauteil1.A4
  N26: U2.A2, U3.A1
  N27: U2.P0, IC4.In_8
  N28: U2.P1, IC4.In_7
  N29: U2.P2, IC4.In_6
  N30: U2.P3, IC4.In_5
  N31: U2.P4, IC4.In_4
  N32: U2.P5, IC4.In_3
  N33: U2.P6, IC4.In_2
  N34: U2.P7, IC4.In_1
  N35: U3.P0, IC5.In_8
  N36: U3.P1, IC5.In_7
  N37: U3.P2, IC5.In_6
  N38: U3.P3, IC5.In_5
  N39: U3.P4, IC5.In_4
  N40: U3.P5, IC5.In_3
  N41: U3.P6, IC5.In_2
  N42: U3.P7, IC5.In_1
  N43: IC3.Out_8, R3.Pin_1
  N44: IC3.Out_7, R2.Pin_1
  N45: IC3.Out_6, R4.Pin_1
  N46: IC3.Out_5, R5.Pin_1

custom parts:
  Niren can bus module: Niren can bus module availabe on ebay and others. Pcb view assumes that you unsolder the 7 pin header and resolder it on the bottom of the module to connect to the pcb. The two jumpers and the can bus connector remain on the top of the board and don't appear in pcb view.
