# Fritzing sketch CAN-BUS-Weichendecoder-Weiche (saved by Fritzing 0.9.9b)
breadboards: 1

parts:
  Bauteil1 = Arduino Nano (Rev3.0)
  IC1 = ULN2803A [package=THT]
  IC2 = ULN2803A [package=THT]  # not connected
  D1 = LED_BARGRAPH_10 [package=led_bargaph_10]
  R1 = RPACK* [package=rpack-sip-pth-5]
  R2 = RPACK* [package=rpack-sip-pth-5]

nets:
  N1: Bauteil1.D3, IC1.In_1, D1.A_A
  N2: Bauteil1.D4, IC1.In_2, D1.B_A
  N3: Bauteil1.D5, IC1.In_3, D1.C_A
  N4: Bauteil1.D6, IC1.In_4
  N5: Bauteil1.D7, IC1.In_5
  N6: Bauteil1.5V, R1.1, R2.1
  N7: D1.J_C, R2.2
  N8: D1.I_C, R2.3
  N9: D1.H_C, R2.4
  N10: D1.G_C, R2.5
  N11: D1.F_C, R2.6
  N12: D1.E_C, R1.6
  N13: D1.D_C, R1.5
  N14: D1.C_C, R1.4
  N15: D1.B_C, R1.3
  N16: D1.A_C, R1.2
